# Fritzing sketch RocketLeagueTicker (saved by Fritzing 0.9.3b)
breadboards: 1

parts:
  Raspberry_Pi_1 = Raspberry Pi 3 [part_number=RPI-3-V1.2]
  U2 = LCD-16X2 [package=lcd-16x2]
  R1 = Rotary Potentiometer (Small) [maximum_resistance=100kΩ package=THT]
  LED1 = LED - 5mm [color="Red (633nm)" package="5 mm [THT]"]
  R2 = Resistor [tolerance=±5% resistance=220 package="2010 [SMD]"]
  R3 = Resistor [tolerance=±5% resistance=220 package="2010 [SMD]"]
  LED2 = LED - 5mm [color="Red (633nm)" package="5 mm [THT]"]
  R4 = Resistor [tolerance=±5% resistance=220 package="2010 [SMD]"]
  LED3 = LED - 5mm [color="Red (633nm)" package="5 mm [THT]"]
  LED4 = LED - 5mm [color="Red (633nm)" package="5 mm [THT]"]
  R5 = Resistor [tolerance=±5% resistance=220 package="2010 [SMD]"]
  S1 = Pushbutton [package="[SMD]"]
  S2 = Pushbutton [package="[SMD]"]
  R6 = Resistor [tolerance=±5% resistance=220 package="2010 [SMD]"]
  LED5 = LED - 5mm [color="Red (633nm)" package="5 mm [THT]"]
  LED6 = LED - 5mm [color="Red (633nm)" package="5 mm [THT]"]
  R7 = Resistor [tolerance=±5% resistance=220 package="2010 [SMD]"]

nets:
  N1: Raspberry_Pi_1.GPIO4, U2.DB5
  N2: Raspberry_Pi_1.GPIO17, U2.DB7
  N3: Raspberry_Pi_1.GPIO5, R7.Pin_1
  N4: Raspberry_Pi_1.GPIO6, R6.Pin_1
  N5: Raspberry_Pi_1.GPIO13, S2.Pin_1, S2.Pin_2
  N6: Raspberry_Pi_1.GPIO19, S1.Pin_1, S1.Pin_2
  N7: Raspberry_Pi_1.GPIO26, LED4.anode, R5.Pin_0
  N8: Raspberry_Pi_1.GPIO21, R2.Pin_1
  N9: Raspberry_Pi_1.GPIO20, R3.Pin_1
  N10: Raspberry_Pi_1.GPIO16, R4.Pin_1
  N11: Raspberry_Pi_1.GND, U2.RS
  N12: Raspberry_Pi_1.GPIO23, U2.E
  N13: Raspberry_Pi_1.GPIO18, U2.DB4
  N14: Raspberry_Pi_1.GPIO14, U2.DB6
  5V: Raspberry_Pi_1.5V, U2.VSS, U2.VDD, U2.R_W, U2.A, U2.K, R1.leg1, R1.leg2, LED1.cathode, LED2.cathode, LED3.cathode, LED4.cathode, S1.Pin_3, S1.Pin_4, S2.Pin_3, S2.Pin_4, LED5.cathode, LED6.cathode
  N15: U2.VO, R1.wiper
  N16: LED1.anode, R2.Pin_0
  N17: R3.Pin_0, LED2.anode
  N18: R4.Pin_0, LED3.anode
  N19: R6.Pin_0, LED5.anode
  N20: LED6.anode, R7.Pin_0
